# Fritzing sketch 2023_power_circuit (saved by Fritzing 0.9.10b)

parts:
  BAT1 = Battery 12V [package=battcom_20mm_pth]  # not connected
  BLDC1 = CTRE Falcon 500 [part_number=19-708850]
  BLDC2 = CTRE Falcon 500 [part_number=19-708850]
  Mini_Power_Module1 = REV Mini Power Module [form="♀ (female)" package=THT]
  ctrl1 = rev_spark_max [part_number=rev-11-2158]
  ctrl2 = rev_spark_max [part_number=rev-11-2158]
  CANcoder1 = CTRE CANcoder [package=THT]
  BLDC4 = CTRE Falcon 500 [part_number=19-708850]
  BLDC5 = CTRE Falcon 500 [part_number=19-708850]
  BLDC6 = CTRE Falcon 500 [part_number=19-708850]
  CB1 = Thermal Circuit Breaker [package=waterproof]  # not connected
  Pigeon_2_1 = CTRE Pigeon 2.0 [package=THT]
  775-Pro_Brushed_Motor1 = 775-Pro Brushed Motor [form="♀ (female)" package=THT]
  775-Pro_Brushed_Motor2 = 775-Pro Brushed Motor [form="♀ (female)" package=THT]
  CANivore1 = CTRE CANivore [form="♀ (female)" package=THT]
  CANcoder4 = CTRE CANcoder [package=THT]
  CANcoder5 = CTRE CANcoder [package=THT]
  Mod2 = VRM
  cntl1 = roborio_v2
  CANcoder6 = CTRE CANcoder [package=THT]
  RPM1 = rev_rpm
  BLDC7 = CTRE Falcon 500 [part_number=19-708850]
  BLDC8 = CTRE Falcon 500 [part_number=19-708850]
  BLDC9 = CTRE Falcon 500 [part_number=19-708850]
  BLDC10 = CTRE Falcon 500 [part_number=19-708850]
  BLDC11 = CTRE Falcon 500 [part_number=19-708850]
  BLDC12 = CTRE Falcon 500 [part_number=19-708850]
  BLDC13 = CTRE Falcon 500 [part_number=19-708850]
  TBE1 = REV Through Bore Encoder  # not connected
  J1 = Generic female header - 7 pins [form="♀ (female)" package=THT]
  J2 = Generic female header - 3 pins [form="♀ (female)" package=THT]  # not connected
  J3 = Generic female header - 3 pins [form="♀ (female)" package=THT]  # not connected
  PDH1 = rev_pdh
  J5 = Generic female header - 1 pins [form="♀ (female)" package=THT]  # not connected
  J6 = Generic female header - 1 pins [form="♀ (female)" package=THT]  # not connected
  RSL1 = FRC Robot Signal Light [part_number=855PB-B12ME522]  # not connected
  Router1 = Rounter OpenMesh  # not connected
  J8 = Generic female header - 5 pins [form="♀ (female)" package=THT]  # not connected

nets:
  N1: BLDC1.Vin-, PDH1.connector1
  N2: BLDC1.Vin+, PDH1.connector0
  N3: BLDC2.Vin-, PDH1.connector3
  N4: BLDC2.Vin+, PDH1.connector2
  N5: Mini_Power_Module1.5+, CANcoder4.+
  N6: Mini_Power_Module1.5-, CANcoder4.-
  N7: Mini_Power_Module1.4+, Pigeon_2_1.+
  N8: Mini_Power_Module1.4-, Pigeon_2_1.-
  N9: Mini_Power_Module1.3+, CANcoder5.+
  N10: Mini_Power_Module1.3-, CANcoder5.-
  N11: Mini_Power_Module1.2+, Mod2.In12V
  N12: Mini_Power_Module1.2-, Mod2.5V_2A_GND0, Mod2.5V_500mA_GND1, Mod2.InGnd, J1.GND
  N13: Mini_Power_Module1.1+, CANivore1.V+[R]
  N14: Mini_Power_Module1.1-, CANivore1.V-[B]
  N15: Mini_Power_Module1.0+, CANcoder1.+
  N16: Mini_Power_Module1.0-, CANcoder1.-
  N17: Mini_Power_Module1.Input_+, PDH1.connector4
  N18: Mini_Power_Module1.Input_-, PDH1.connector5
  N19: ctrl1.connector0, PDH1.connector12
  N20: ctrl1.connector1, PDH1.connector13
  N21: ctrl1.connector2, 775-Pro_Brushed_Motor1.pin1
  N22: ctrl1.connector3, 775-Pro_Brushed_Motor1.pin2
  N23: ctrl2.connector0, PDH1.connector10
  N24: ctrl2.connector1, PDH1.connector11
  N25: ctrl2.connector2, 775-Pro_Brushed_Motor2.pin1
  N26: ctrl2.connector3, 775-Pro_Brushed_Motor2.pin2
  N27: BLDC4.Vin-, PDH1.connector7
  N28: BLDC4.Vin+, PDH1.connector6
  N29: BLDC5.Vin-, PDH1.connector9
  N30: BLDC5.Vin+, PDH1.connector8
  N31: BLDC6.Vin-, PDH1.connector15
  N32: BLDC6.Vin+, PDH1.connector14
  N33: Mod2.5V_500mA_5V1, J1.V+
  N34: cntl1.connector39, PDH1.connector47
  N35: cntl1.connector40, PDH1.connector46
  N36: CANcoder6.-, PDH1.connector48
  N37: RPM1.connector0, PDH1.connector50
  N38: RPM1.connector1, PDH1.connector51
  N39: BLDC7.Vin-, PDH1.connector38
  N40: BLDC7.Vin+, PDH1.connector39
  N41: BLDC8.Vin-, PDH1.connector36
  N42: BLDC8.Vin+, PDH1.connector37
  N43: BLDC9.Vin-, PDH1.connector34
  N44: BLDC9.Vin+, PDH1.connector35
  N45: BLDC10.Vin-, PDH1.connector32
  N46: BLDC10.Vin+, PDH1.connector33
  N47: BLDC11.Vin-, PDH1.connector30
  N48: BLDC11.Vin+, PDH1.connector31
  N49: BLDC12.Vin-, PDH1.connector28
  N50: BLDC12.Vin+, PDH1.connector29
  N51: BLDC13.Vin-, PDH1.connector26
  N52: BLDC13.Vin+, PDH1.connector27

custom parts:
  Battery 12V: Battery Holders Various common sizes : AA, AAA, 20mm coin cell and 12mm coin cell.
  CTRE Falcon 500: The Falcon 500 powered by Talon FX is a brushless motor with an integrated motor controller and high-resolution encoder, custom designed specifically for the FIRST Robotics Competition, through a collaboration between Cross the Road Electronics and VEX Robotics.
  REV Mini Power Module: Generic female header
  Thermal Circuit Breaker: Cooper Bussman P/N CB185-120, CB185F-120, CB285-120 CB285F-120, CB285120F or Optifuse P/N 153120, 253120
  CTRE Pigeon 2.0: Generic single row SMD female header
  REV Through Bore Encoder: The REV Through Bore Encoder is specifically designed with the end user in mind, allowing teams to place sensors in the locations closest to the rotation that they wish to measure. This rotary sensor measures both relative and absolute position through its ABI quadrature output and its absolute position pulse output. Mounting an encoder has never been easier with a 1/2in Hex Through Bore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
  Generic female header - 7 pins: Generic female header
  Generic female header - 3 pins: Generic female header
  Generic female header - 1 pins: Generic female header
  Generic female header - 1 pins: Generic female header
  FRC Robot Signal Light: Panel Mount Beacon,12V AC/DC,45 mm Panel Mounting LED,Amber,22.5 mm Round Mounting Hole Used as: R709 *ROBOTS must have a signal light. ROBOTS must use at least 1, but no more than 2, diagnostic ROBOT Signal Light (RSL) (P/N 855PB-B12ME522). Any RSL must be: A. mounted on the ROBOT such that it is easily visible while standing 3 ft. (~ 100 cm) in front of the ROBOT, B. connected to the “RSL”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
  Generic female header - 5 pins: Generic female header
