# Fritzing sketch dcmp_2023_Power (saved by Fritzing 0.9.10b)

parts:
  BAT1 = Battery 12V [package=battcom_20mm_pth]
  BLDC1 = CTRE Falcon 500 [part_number=19-708850]
  BLDC2 = CTRE Falcon 500 [part_number=19-708850]
  Mini_Power_Module1 = REV Mini Power Module [form="♀ (female)" package=THT]
  ctrl1 = rev_spark_max [part_number=rev-11-2158]
  ctrl2 = rev_spark_max [part_number=rev-11-2158]
  CANcoder1 = CTRE CANcoder [package=THT]
  BLDC4 = CTRE Falcon 500 [part_number=19-708850]
  BLDC5 = CTRE Falcon 500 [part_number=19-708850]
  BLDC6 = CTRE Falcon 500 [part_number=19-708850]
  CB1 = Thermal Circuit Breaker [package=waterproof]
  Pigeon_2_1 = CTRE Pigeon 2.0 [package=THT]
  775-Pro_Brushed_Motor1 = 775-Pro Brushed Motor [form="♀ (female)" package=THT]
  775-Pro_Brushed_Motor2 = 775-Pro Brushed Motor [form="♀ (female)" package=THT]
  CANivore1 = CTRE CANivore [form="♀ (female)" package=THT]
  CANcoder4 = CTRE CANcoder [package=THT]
  CANcoder5 = CTRE CANcoder [package=THT]
  Mod2 = VRM
  cntl1 = roborio_v2
  CANcoder6 = CTRE CANcoder [package=THT]
  RPM1 = rev_rpm
  BLDC7 = CTRE Falcon 500 [part_number=19-708850]
  BLDC8 = CTRE Falcon 500 [part_number=19-708850]
  BLDC9 = CTRE Falcon 500 [part_number=19-708850]
  BLDC10 = CTRE Falcon 500 [part_number=19-708850]
  BLDC11 = CTRE Falcon 500 [part_number=19-708850]
  BLDC12 = CTRE Falcon 500 [part_number=19-708850]
  BLDC13 = CTRE Falcon 500 [part_number=19-708850]
  J1 = Generic female header - 7 pins [form="♀ (female)" package=THT]
  PDH1 = rev_pdh
  Part2 = LilyPad LED  # not connected
  Part3 = LilyPad LED  # not connected
  Part4 = LilyPad LED  # not connected
  Part5 = LilyPad LED  # not connected
  Part6 = LilyPad LED  # not connected
  Part7 = LilyPad LED  # not connected
  Part8 = LilyPad LED  # not connected
  Part9 = LilyPad LED
  JP1 = APP SB50 [package=sb50]
  JP2 = APP SB50 [package=sb50]
  Part11 = LilyPad LED  # not connected
  Part12 = LilyPad LED  # not connected
  Part13 = LilyPad LED  # not connected
  Part14 = LilyPad LED  # not connected
  Part16 = LilyPad LED  # not connected
  J4 = Generic female header - 2 pins [form="♀ (female)" package=THT]
  J5 = Generic female header - 5 pins [form="♀ (female)" package=THT]
  M1 = RioRand LM2596

nets:
  N1: BAT1.+, JP2.2
  N2: BAT1.-, JP2.1
  N3: BLDC1.Vin-, PDH1.connector1
  N4: BLDC1.Vin+, PDH1.connector0
  N5: BLDC2.Vin-, PDH1.connector3
  N6: BLDC2.Vin+, PDH1.connector2
  N7: Mini_Power_Module1.5+, CANcoder4.+
  N8: Mini_Power_Module1.5-, CANcoder4.-
  N9: Mini_Power_Module1.4+, Pigeon_2_1.+
  N10: Mini_Power_Module1.4-, Pigeon_2_1.-
  N11: Mini_Power_Module1.3+, CANcoder5.+
  N12: Mini_Power_Module1.3-, CANcoder5.-
  N13: Mini_Power_Module1.2+, Mod2.In12V
  N14: Mini_Power_Module1.2-, Mod2.5V_2A_GND0, Mod2.5V_500mA_GND1, Mod2.InGnd, J1.GND
  N15: Mini_Power_Module1.1+, CANivore1.V+[R]
  N16: Mini_Power_Module1.1-, CANivore1.V-[B]
  N17: Mini_Power_Module1.0+, CANcoder1.+
  N18: Mini_Power_Module1.0-, CANcoder1.-
  N19: Mini_Power_Module1.Input_+, PDH1.connector4
  N20: Mini_Power_Module1.Input_-, PDH1.connector5
  N21: ctrl1.connector0, PDH1.connector12
  N22: ctrl1.connector1, PDH1.connector13
  N23: ctrl1.connector2, 775-Pro_Brushed_Motor1.pin1
  N24: ctrl1.connector3, 775-Pro_Brushed_Motor1.pin2
  N25: ctrl2.connector0, PDH1.connector10
  N26: ctrl2.connector1, PDH1.connector11
  N27: ctrl2.connector2, 775-Pro_Brushed_Motor2.pin1
  N28: ctrl2.connector3, 775-Pro_Brushed_Motor2.pin2
  N29: BLDC4.Vin-, PDH1.connector7
  N30: BLDC4.Vin+, PDH1.connector6
  N31: BLDC5.Vin-, PDH1.connector9
  N32: BLDC5.Vin+, PDH1.connector8
  N33: BLDC6.Vin-, PDH1.connector15
  N34: BLDC6.Vin+, PDH1.connector14
  N35: CB1.1, PDH1.connector45
  N36: CB1.2, JP1.2
  N37: Mod2.5V_500mA_5V1, J1.V+
  N38: cntl1.connector39, PDH1.connector47
  N39: cntl1.connector40, PDH1.connector46
  N40: CANcoder6.-, PDH1.connector48
  N41: RPM1.connector0, PDH1.connector50
  N42: RPM1.connector1, PDH1.connector51
  N43: BLDC7.Vin-, PDH1.connector38
  N44: BLDC7.Vin+, PDH1.connector39
  N45: BLDC8.Vin-, PDH1.connector36
  N46: BLDC8.Vin+, PDH1.connector37
  N47: BLDC9.Vin-, PDH1.connector34
  N48: BLDC9.Vin+, PDH1.connector35
  N49: BLDC10.Vin-, PDH1.connector32
  N50: BLDC10.Vin+, PDH1.connector33
  N51: BLDC11.Vin-, PDH1.connector30
  N52: BLDC11.Vin+, PDH1.connector31
  N53: BLDC12.Vin-, PDH1.connector28
  N54: BLDC12.Vin+, PDH1.connector29
  N55: BLDC13.Vin-, PDH1.connector26
  N56: BLDC13.Vin+, PDH1.connector27
  N57: PDH1.connector16, Part9.+
  N58: PDH1.connector17, Part9.-
  N59: PDH1.connector24, M1.Pin_1
  N60: PDH1.connector25, M1.Pin_2
  N61: PDH1.connector44, JP1.1
  N62: PDH1.connector52, J4.V-
  N63: PDH1.connector53, J4.V+
  N64: J5.DC-Power, M1.Pin_3, M1.Pin_4

notes:
  Right Arm
  Rotation
  PDH 7
  CAN 13
  Front Right
  PDH 4
  CAN 3
  PDH 3
  CAN 4
  Drive
  PDH 6
  CAN 16
  CAN 15
  PDH 5
  Intake 1
  PDH 1
  Back Right
  CAN 5
  PDH 0
  CAN 6
  Left Arm
  PDH 13
  CAN 14
  Arm
  PDH 14
  CAN 18
  Extension
  CAN 17
  Wrist
  PDH 15
  CAN 1
  PDH 17
  PDH 16
  Front Left
  CAN 2
  PDH 2
  Intake 2
  Back Left
  CAN 8
  PDH 18
  CAN 7
  PDH 19
  RoboRIO
  PDH 20
  Front Left CANcoder
  PDH 21
  CAN 9
  PDH 22
  CAN 10
  MPM 5
  Front Right CANcoder
  CAN 20
  MPM 4
  Gyroscope
  CAN 11
  MPM 3
  Back Right CANcoder
  MPM 2
  Back Left CANcoder
  CAN 12
  MPM 0
  MPM 1
  CANivore
  Signal LEDs
  PDH 8
  VRM 5V 500mA
  Ethernet Switch
  PDH 23
  Hour Meter
  PDH 12
  Buck–Boost Converter
  Mini PC
  775pro Motor
  12V Battery

custom parts:
  Battery 12V: Battery Holders Various common sizes : AA, AAA, 20mm coin cell and 12mm coin cell.
  CTRE Falcon 500: The Falcon 500 powered by Talon FX is a brushless motor with an integrated motor controller and high-resolution encoder, custom designed specifically for the FIRST Robotics Competition, through a collaboration between Cross the Road Electronics and VEX Robotics.
  REV Mini Power Module: Generic female header
  Thermal Circuit Breaker: Cooper Bussman P/N CB185-120, CB185F-120, CB285-120 CB285F-120, CB285120F or Optifuse P/N 153120, 253120
  CTRE Pigeon 2.0: Generic single row SMD female header
  Generic female header - 7 pins: Generic female header
  APP SB50: Anderson Power Products SB®50 Connectors feature a one-piece plastic housing using stainless steel springs to hold low-resistance contacts in place. These connectors work with wire contacts up to 6AWG (10mm²) as well as PCB and busbar contacts. The genderless design mates with itself and has a plated through-hole mounting style. Anderson SB®50 Connectors are UL-rated for hot plugging up to 50A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
  Generic female header - 2 pins: Generic female header
  Generic female header - 5 pins: Generic female header
