# Fritzing sketch banner_sensor_hack (saved by Fritzing 0.9.10b)

parts:
  Q2 = MOSFET-NCHANNEL [package=to220v]
  Part2 = LilyPad LED  # not connected
  WRIST_ROTATION_MOTOR = Generic female header - 4 pins [form="♀ (female)" package=THT]
  J4 = Generic female header - 3 pins [form="♀ (female)" package=THT]
  J8 = Generic female header - 3 pins [form="♀ (female)" package=THT]
  Q1 = MOSFET-NCHANNEL [package=to220v]
  Part3 = LilyPad LED  # not connected
  Part4 = LilyPad LED  # not connected
  Part5 = LilyPad LED  # not connected
  Part6 = LilyPad LED  # not connected
  Part7 = LilyPad LED  # not connected
  Part8 = LilyPad LED  # not connected
  Part9 = LilyPad LED
  J10 = Generic female header - 3 pins [form="♀ (female)" package=THT]
  J11 = Generic female header - 3 pins [form="♀ (female)" package=THT]

nets:
  N1: Q2.G, J8.Out
  N2: Q2.D, WRIST_ROTATION_MOTOR.Forward
  N3: Q2.S, WRIST_ROTATION_MOTOR.GND#1
  N4: WRIST_ROTATION_MOTOR.GND#2, Q1.S
  N5: WRIST_ROTATION_MOTOR.Reverse, Q1.D
  N6: J4.GND, J10.pin2
  N7: J4.V+, J11.pin2
  N8: J4.Out, Q1.G
  N9: J8.GND, J10.pin3
  N10: J8.V+, J11.pin3
  N11: Part9.+, J11.pin1
  N12: Part9.-, J10.pin1

notes:
  5V Supply
  GND
  Soruce
  Gate
  Drain
  MOSFET Transistors
  {
  Transistor Pins
  Signaling LEDs

custom parts:
  Generic female header - 4 pins: Generic female header
  Generic female header - 3 pins: Generic female header
  Generic female header - 3 pins: Generic female header
  Generic female header - 3 pins: Generic female header
