# Fritzing sketch vabla_2023_data (saved by Fritzing 0.9.10b)

parts:
  CANivore1 = CTRE CANivore [form="♀ (female)" package=THT]
  CAN_6_-_Back_Right_Drive = CTRE Falcon 500 [part_number=19-708850]
  CAN_14_-_Right_Arm_Rotation = CTRE Falcon 500 [part_number=19-708850]
  CANcoder1 = CTRE CANcoder [package=THT]
  CAN_5_-_Back_Right_Rotation = CTRE Falcon 500 [part_number=19-708850]
  CAN_4_Front_Right_Drive = CTRE Falcon 500 [part_number=19-708850]
  CAN_3_Front_Right_Rotation = CTRE Falcon 500 [part_number=19-708850]
  CANcoder2 = CTRE CANcoder [package=THT]
  Pigeon_2_1 = CTRE Pigeon 2.0 [package=THT]
  CAN_13_Left_Arm_Rotation = CTRE Falcon 500 [part_number=19-708850]
  CAN_2_Front_Left = CTRE Falcon 500 [part_number=19-708850]
  CAN_1_Front_Left = CTRE Falcon 500 [part_number=19-708850]
  CANcoder3 = CTRE CANcoder [package=THT]
  CAN_8_Back_Left = CTRE Falcon 500 [part_number=19-708850]
  CAN_7_Back_Right1 = CTRE Falcon 500 [part_number=19-708850]
  cntl1 = roborio_v2
  ctrl1 = rev_spark_max [part_number=rev-11-2158]
  ctrl2 = rev_spark_max [part_number=rev-11-2158]
  PDH1 = rev_pdh
  Router1 = Rounter OpenMesh
  RSL2 = FRC Robot Signal Light [part_number=855PB-B12ME522]
  J2 = Generic female header - 7 pins [form="♀ (female)" package=THT]
  TBE2 = REV Through Bore Encoder
  CAM3 = Limelight 2plus
  CAM4 = Limelight 2plus
  RPM1 = rev_rpm
  R1 = Resistor [package=THT]
  CAN_1_Front_Left1 = CTRE Falcon 500 [part_number=19-708850]
  CAN_1_Front_Left2 = CTRE Falcon 500 [part_number=19-708850]
  CANcoder4 = CTRE CANcoder [package=THT]
  R2 = Resistor [package=THT]

nets:
  N1: CANivore1.CANL[G], CAN_6_-_Back_Right_Drive.CANL0
  N2: CANivore1.CANH[Y], CAN_6_-_Back_Right_Drive.CANH1#3
  N3: CAN_6_-_Back_Right_Drive.CANL1, CAN_14_-_Right_Arm_Rotation.CANL0
  N4: CAN_6_-_Back_Right_Drive.CANH1#5, CAN_14_-_Right_Arm_Rotation.CANH1#3
  N5: CAN_14_-_Right_Arm_Rotation.CANL1, CANcoder1.IN-CANL[G]
  N6: CAN_14_-_Right_Arm_Rotation.CANH1#5, CANcoder1.IN-CANH[Y]
  N7: CANcoder1.OUT-CANH[Y], CAN_5_-_Back_Right_Rotation.CANH1#3
  N8: CANcoder1.OUT-CANL[G], CAN_5_-_Back_Right_Rotation.CANL0
  N9: CAN_5_-_Back_Right_Rotation.CANL1, CAN_4_Front_Right_Drive.CANL0
  N10: CAN_5_-_Back_Right_Rotation.CANH1#5, CAN_4_Front_Right_Drive.CANH1#3
  N11: CAN_4_Front_Right_Drive.CANL1, CANcoder2.IN-CANL[G]
  N12: CAN_4_Front_Right_Drive.CANH1#5, CANcoder2.IN-CANH[Y]
  N13: CAN_3_Front_Right_Rotation.CANL0, CANcoder2.OUT-CANL[G]
  N14: CAN_3_Front_Right_Rotation.CANH1#3, CANcoder2.OUT-CANH[Y]
  N15: CAN_3_Front_Right_Rotation.CANL1, Pigeon_2_1.IN-CANL[G]
  N16: CAN_3_Front_Right_Rotation.CANH1#5, Pigeon_2_1.IN-CANH[Y]
  N17: Pigeon_2_1.OUT-CANH[Y], CAN_13_Left_Arm_Rotation.CANH1#3
  N18: Pigeon_2_1.OUT-CANL[G], CAN_13_Left_Arm_Rotation.CANL0
  N19: CAN_13_Left_Arm_Rotation.CANL1, CAN_2_Front_Left.CANL0
  N20: CAN_13_Left_Arm_Rotation.CANH1#5, CAN_2_Front_Left.CANH1#3
  N21: CAN_2_Front_Left.CANL1, CANcoder3.IN-CANL[G]
  N22: CAN_2_Front_Left.CANH1#5, CANcoder3.IN-CANH[Y]
  N23: CAN_1_Front_Left.CANL0, CANcoder3.OUT-CANL[G]
  N24: CAN_1_Front_Left.CANH1#3, CANcoder3.OUT-CANH[Y]
  N25: CAN_1_Front_Left.CANL1, CAN_1_Front_Left1.CANL0
  N26: CAN_1_Front_Left.CANH1#5, CAN_1_Front_Left1.CANH1#3
  N27: CAN_8_Back_Left.CANL0, PDH1.connector40
  N28: CAN_8_Back_Left.CANH1#3, PDH1.connector41
  N29: CAN_8_Back_Left.CANL1, CAN_7_Back_Right1.CANL0
  N30: CAN_8_Back_Left.CANH1#5, CAN_7_Back_Right1.CANH1#3
  N31: CAN_7_Back_Right1.CANL1, R1.Pin_0
  N32: CAN_7_Back_Right1.CANH1#5, R1.Pin_1
  N33: cntl1.connector0, ctrl1.connector7
  N34: cntl1.connector1, ctrl1.connector6
  N35: cntl1.connector9, TBE2.GND
  N36: cntl1.connector10, TBE2.V
  N37: cntl1.connector11, TBE2.A
  N38: cntl1.connector41, RSL2.anode0
  N39: cntl1.connector42, RSL2.common_cathode
  N40: cntl1.connector144, J2.1
  N41: ctrl1.connector4, ctrl2.connector6
  N42: ctrl1.connector5, ctrl2.connector7
  N43: ctrl2.connector4, PDH1.connector43
  N44: ctrl2.connector5, PDH1.connector42
  N45: Router1.ETH_right, RPM1.connector2
  N46: J2.3, CAM3.ETH0
  N47: J2.4, CAM4.ETH0
  N48: CAN_1_Front_Left1.CANL1, CANcoder4.IN-CANL[G]
  N49: CAN_1_Front_Left1.CANH1#5, CANcoder4.IN-CANH[Y]
  N50: CAN_1_Front_Left2.CANL0, CANcoder4.OUT-CANL[G]
  N51: CAN_1_Front_Left2.CANH1#3, CANcoder4.OUT-CANH[Y]
  N52: CAN_1_Front_Left2.CANL1, R2.Pin_0
  N53: CAN_1_Front_Left2.CANH1#5, R2.Pin_1

notes:
  Back Right
  CAN 6
  Drive
  Right Arm
  Rotation
  CAN 14
  CAN 4
  CAN 5
  Front Right
  CAN 3
  Left Arm
  CAN 13
  CAN 1
  Front Left
  CAN 2
  CAN 17
  Wrist Rotation
  CAN 20
  CAN 15
  Manipulator 1
  CAN 16
  Manipulator 2
  Arm Extension
  CAN 18
  Terminating
  120Ω
  Resistor
  Ethernet Switch
  Limelight Front
  Limelight Rear
  Radio
  CAN 9
  CANcoder
  CAN 11
  CAN 10
  Back Left
  CAN 7
  CAN 8
  CAN 12
  Through Bore Encoder
  Robot Signal Light

custom parts:
  CTRE Falcon 500: The Falcon 500 powered by Talon FX is a brushless motor with an integrated motor controller and high-resolution encoder, custom designed specifically for the FIRST Robotics Competition, through a collaboration between Cross the Road Electronics and VEX Robotics.
  CTRE Pigeon 2.0: Generic single row SMD female header
  FRC Robot Signal Light: Panel Mount Beacon,12V AC/DC,45 mm Panel Mounting LED,Amber,22.5 mm Round Mounting Hole Used as: R709 *ROBOTS must have a signal light. ROBOTS must use at least 1, but no more than 2, diagnostic ROBOT Signal Light (RSL) (P/N 855PB-B12ME522). Any RSL must be: A. mounted on the ROBOT such that it is easily visible while standing 3 ft. (~ 100 cm) in front of the ROBOT, B. connected to the “RSL”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
  Generic female header - 7 pins: Generic female header
  REV Through Bore Encoder: The REV Through Bore Encoder is specifically designed with the end user in mind, allowing teams to place sensors in the locations closest to the rotation that they wish to measure. This rotary sensor measures both relative and absolute position through its ABI quadrature output and its absolute position pulse output. Mounting an encoder has never been easier with a 1/2in Hex Through Bore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
  Limelight 2plus: Limelight makes reliable FRC vision accessible to all teams, regardless of programming ability and time constraints. Vision has never been easier. Limelight 2+ takes the Einstein-proven Limelight 2 and perfects it. Its internals have been redesigned to: - Reduce power consumption by up to 50% - Eliminate the LED "warm-up" period. - Further improve low voltage performance, dropping the brownout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
  Resistor: A generic 5-band resistor (0.25W)
